# Fritzing sketch HB-MR-MOIST-SENS-SW2 (saved by Fritzing 0.9.4)
circuit board: 5.5cm x 5.5cm
breadboards: 1

parts:
  Power_In = Screw terminal - 2 pins [package=THT]
  Bauteil2 = Arduino Pro Mini v13
  R1 = Resistor [tolerance=±5% resistance=330 package=THT]
  Config = Momentary Switch [package=ksa_sealed_tac_switch]
  LED = LED - 3mm [color="Red (633nm)" package="3 mm [THT]"]
  J2 = female pin header, 1 pin [form="♀ (female)"]
  Pad12 = Pad [width=1.4 height=4 connect=center]
  Pad13 = Pad [width=1.4 height=4 connect=center]
  Pad14 = Pad [width=1.4 height=4 connect=center]
  Pad15 = Pad [width=1.4 height=4 connect=center]  # not connected
  Pad16 = Pad [width=1.4 height=4 connect=center]
  Pad17 = Pad [width=1.4 height=4 connect=center]  # not connected
  Pad18 = Pad [width=1.4 height=4 connect=center]  # not connected
  Pad19 = Pad [width=1.4 height=4 connect=center]  # not connected
  Pad20 = Pad [width=1.4 height=4 connect=center]  # not connected
  Pad21 = Pad [width=1.4 height=4 connect=center]  # not connected
  Pad22 = Pad [width=1.4 height=4 connect=center]  # not connected
  Pumpe = screw terminal, 2 pins
  LED_Bel = screw terminal, 2 pins
  TIP120 = Basic FET P-Channel [package="TO220 [THT]"]
  TIP120_2 = Basic FET P-Channel [package="TO220 [THT]"]
  D1 = Rectifier Diode [part_number=1N4001 package="300 mil [THT]"]
  D2 = Rectifier Diode [part_number=1N4001 package="300 mil [THT]"]
  J2_2 = female pin header, 3 pins [form="♀ (female)"]
  R2 = Resistor [tolerance=±5% resistance=2.2k package=THT]
  R3 = Resistor [tolerance=±5% resistance=2.2k package=THT]
  J1 = female pin header, 3 pins [form="♀ (female)"]
  Sensors = female pin header, 3 pins [form="♀ (female)"]
  J3 = female pin header, 4 pins [form="♀ (female)"]
  Sensor1 = female pin header, 3 pins [form="♀ (female)"]
  J4 = female pin header, 4 pins [form="♀ (female)"]

nets:
  N1: Power_In.pin1, Bauteil2.RAW, J2_2.pin3, J1.pin3
  N2: Power_In.pin2, Bauteil2.GND, Config.3, Config.4, LED.cathode, TIP120.source, TIP120_2.source, Sensors.pin1, J3.pin2, J3.pin4, Sensor1.pin1, J4.pin1
  N3: Bauteil2.VCC, J2_2.pin1, J1.pin1, J4.pin2
  N4: Bauteil2.A4, J4.pin4
  N5: Bauteil2.A5, J4.pin3
  N6: Bauteil2.A1, Sensors.pin3
  N7: Bauteil2.A0, Sensor1.pin3
  N8: Bauteil2.D9_PWM, J3.pin1
  N9: Bauteil2.D8, Config.1, Config.2
  N10: Bauteil2.D7, J3.pin3
  N11: Bauteil2.D6_PWM, R2.Pin_1
  N12: Bauteil2.D5_PWM, Sensors.pin2, Sensor1.pin2
  N13: Bauteil2.D4, R1.Pin_1
  N14: Bauteil2.D3_PWM, R3.Pin_1
  N15: R1.Pin_0, LED.anode
  N16: J2.pin1, Pad13.pad
  N17: Pad12.pad, Pad14.pad, Pad16.pad
  N18: Pumpe.pin1, D2.cathode, J2_2.pin2
  N19: Pumpe.pin2, TIP120_2.drain, D2.anode
  N20: LED_Bel.pin1, D1.cathode, J1.pin2
  N21: LED_Bel.pin2, TIP120.drain, D1.anode
  N22: TIP120.gate, R3.Pin_0
  N23: TIP120_2.gate, R2.Pin_0

notes:
  ARDUINO Pro Mini
  CSN
  GDO0
  868 mHz
  GDO2
  SO
  SCLK
  SI
  GND
  3.3V
  ANT
  CC1101
  V1.0
  (C)2021 netprog2019
  13.05.2021
  GND GND VCC RXI TXO DTR
  3.3V / 8mHz
  GND VCC
  3.3V |  VCC
  3.4 - 9V
  Switch 1
  Switch 2
  HB-MOIST-SENS-SW2
  Moistsensor mit 2-fach Aktor
  A-In 3.3V GND
  TA1 | TA2
  AskSinPP
  SDA SCL 3.3V GND
  GND 3.3V SCl SDA
